# Fritzing sketch RFID (saved by Fritzing 0.9.5d)
breadboards: 1

parts:
  125_kHz_RFID = RDM6300
  2N3904 = NPN-Transistor [package="TO92 [THT]"]
  Part1 = Arduino Pro Mini (5V)
  C3 = Ceramic Capacitor [capacitance=10nF package="100 mil [THT, multilayer]"]
  ANTENNA = Inductor [package="400 mil [THT]"]
  R1 = Resistor [tolerance=±5% resistance=10k package=THT]
  CLONE_BUTTON = Pushbutton [package="[THT]"]

nets:
  TX_RFID: 125_kHz_RFID.TX, Part1.RXI
  ANT1/GND: 125_kHz_RFID.GND, 125_kHz_RFID.ANT1, 2N3904.E, 2N3904.C, Part1.GND, C3.0, C3.1, ANTENNA.pin_1, CLONE_BUTTON.Pin_2
  RFID_POWER: 125_kHz_RFID.+5V#61, Part1.D7
  ANT2: 125_kHz_RFID.ANT2, ANTENNA.pin_0
  N1: 2N3904.B, R1.Pin_1
  ANT_EMU: Part1.D9, R1.Pin_0
  BTN_CLONE: Part1.D4, CLONE_BUTTON.Pin_3, CLONE_BUTTON.Pin_4

custom parts:
  RDM6300: 125 kHz RFID module (serial interface)
